# Fritzing sketch Klingel (saved by Fritzing 0.9.2b)
circuit board: 32.042cm x 16.6024cm

parts:
  Adu_Uno = Arduino Uno (Rev3)
  Sound_Ding = Audio FX Sound Board
  LED2 = LED - 5mm [color="Green (565nm)" package="5 mm [THT]"]
  Bauteil2 = Max Powe RGB LED Kit
  Grove1 = Grove OLED 128x96
  Bauteil3 = RFID-RC522-v2
  JP1 = Header 8 [package=1x08_smd]
  JP2 = Header 8 [package=1x08_smd]

nets:
  N1: Adu_Uno.D10_PWM/SS, Bauteil3.IRQ, Bauteil3.NSS, JP1.4, JP2.4
  N2: Adu_Uno.D11_PWM/MOSI, Bauteil3.MOSI, JP1.3, JP2.3
  N3: Adu_Uno.D12/MISO, Bauteil3.MISO, JP1.2, JP2.2
  N4: Adu_Uno.D13/SCK, Bauteil3.SCK, JP1.1, JP2.1
  GND: Adu_Uno.GND, Sound_Ding.GND, LED2.cathode, Bauteil2.GND, Grove1.GND, Bauteil3.GND, JP1.5, JP2.5
  N5: Adu_Uno.A4/SDA, Grove1.SDA
  N6: Adu_Uno.A5/SCL, Grove1.SCL
  N7: Adu_Uno.D2, LED2.anode, JP1.6, JP2.6
  N8: Adu_Uno.D3_PWM, Sound_Ding.0
  N9: Adu_Uno.D5_PWM, Bauteil3.RST, JP1.7, JP2.7
  N10: Adu_Uno.D6_PWM, Bauteil2.CONTROL
  N11: Adu_Uno.D7, Bauteil2.VCC
  3V3: Adu_Uno.3V3, Sound_Ding.VIN, Bauteil3.3.3V, JP1.8, JP2.8
  5V: Adu_Uno.5V, Grove1.VCC

notes:
  Kabel zur Tür

custom parts:
  Audio FX Sound Board: The Adafruit Sound Board, the fastest way to add audio effects to a project!
  Max Powe RGB LED Kit: Description: Infrared LEDs are awesome. Along with an IR receiver they can be used for remote control and even basic remote data communication. The only problem is that your Arduino won't drive them to their full potential. The Max Power IR LED kit solves this problem by providing you with everything you need to drive a 950nm IR LED properly. Simply solder together this easy through-hole kit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
  RFID-RC522-v2: A simple China made RFID-RC522 Reader; do check the pin labels, as this is a MFRC522 based clone.
